# Fritzing sketch control tramo meta (saved by Fritzing 0.8.7b)

parts:
  Arduino1 = Arduino Mini (Rev5)
  Transceiver1 = nRF24L01 [package=module]
  J1 = Infrared Proximity Sensor
  S1 = Square Pushbutton
  OLED1 = OLED 128x64 I2C Monochrome Display
  U1 = Voltage Regulator - 5V [package="TO220 [THT]"]
  VCC1 = Battery block 9V
  S2 = Toggle Switch [package=THT]
  LED1 = LED - 5mm [color="Red (633nm)" package="5 mm [THT]"]
  LED2 = LED - 5mm [color="Green (570nm)" package="5 mm [THT]"]
  LED3 = LED - 5mm [color="Orange (612nm)" package="5 mm [THT]"]
  R1 = Resistor [tolerance=±5% resistance=470 package=THT]
  R2 = Resistor [tolerance=±5% resistance=470 package=THT]
  R3 = Resistor [tolerance=±5% resistance=470 package=THT]
  R4 = Resistor [tolerance=±5% resistance=10k package=THT]
  D1 = Rectifier Diode [part_number=1N4001 package="300 mil [THT]"]
  D2 = Rectifier Diode [part_number=1N4001 package="300 mil [THT]"]

nets:
  N1: Arduino1.D3_PWM, S1.leg1, R4.Pin_1
  N2: Arduino1.D4, R1.Pin_1
  N3: Arduino1.D6_PWM, R2.Pin_1
  N4: Arduino1.D7, R3.Pin_1
  5V: Arduino1.5V, J1.Vcc, OLED1.VDD, U1.output_voltage, R4.Pin_0, D1.anode
  N5: Arduino1.A3, J1.Vout
  N6: Arduino1.A2, Transceiver1.CSN
  N7: Arduino1.A1, Transceiver1.CE
  N8: Arduino1.D13, Transceiver1.SCK
  N9: Arduino1.D12, Transceiver1.MISO
  N10: Arduino1.D11_PWM, Transceiver1.MOSI
  N11: Arduino1.A4, OLED1.SDA
  N12: Arduino1.A5, OLED1.SCK
  GND: Arduino1.GND, Transceiver1.GND, J1.GND, S1.leg0, OLED1.GND, U1.GND, VCC1.-, LED1.cathode, LED2.cathode, LED3.cathode
  N13: Transceiver1.VCC, D2.cathode
  N14: U1.input_voltage, S2.L2
  N15: VCC1.+, S2.COM
  N16: LED1.anode, R1.Pin_0
  N17: LED2.anode, R2.Pin_0
  N18: LED3.anode, R3.Pin_0
  N19: D1.cathode, D2.anode

notes:
  A4
  A5
  470 Ohm
  1N4007
  10k
  Arduino Pro Mini
  Sensor reflector Sharp GP2Y0A41SK0F
  7805
  NRFL24L01
  Oled SSD1306

custom parts:
  nRF24L01: nRF24L01 module
