# Fritzing sketch control tramo salida (saved by Fritzing 0.8.7b)

parts:
  Arduino1 = Arduino Mini (Rev5)
  Transceiver1 = nRF24L01 [package=module]
  J1 = Infrared Proximity Sensor
  D1 = Diode [package=diode-1n4001]
  D2 = Diode [package=diode-1n4001]
  S1 = Square Pushbutton
  S2 = Toggle Switch [package=THT]
  S3 = Toggle Switch [package=THT]
  U1 = Voltage Regulator - 5V [package="DPak [SMD]"]
  VCC1 = Battery block 9V
  R1 = Resistor [tolerance=±5% resistance=10k package=THT]
  J2 = Piezo Speaker
  LED1 = LED - 5mm [color="Red (633nm)" package="5 mm [THT]"]
  LED2 = LED - 5mm [color="Red (633nm)" package="5 mm [THT]"]
  LED3 = LED - 5mm [color="Red (633nm)" package="5 mm [THT]"]
  LED4 = LED - 5mm [color="Green (560nm)" package="5 mm [THT]"]
  LED5 = LED - 5mm [color="Orange (612nm)" package="5 mm [THT]"]
  R2 = Resistor [tolerance=±5% resistance=470 package=THT]
  R3 = Resistor [tolerance=±5% resistance=470 package=THT]
  R4 = Resistor [tolerance=±5% resistance=470 package=THT]
  R5 = Resistor [tolerance=±5% resistance=470 package=THT]
  R6 = Resistor [tolerance=±5% resistance=470 package=THT]

nets:
  N1: Arduino1.D2, R2.Pin_1
  N2: Arduino1.D3_PWM, R3.Pin_1
  N3: Arduino1.D4, R4.Pin_1
  N4: Arduino1.D5_PWM, R5.Pin_1
  N5: Arduino1.D6_PWM, R1.Pin_0
  N6: Arduino1.D7, J2.pin2
  N7: Arduino1.D8, R6.Pin_1
  N8: Arduino1.A3, J1.Vout
  N9: Arduino1.A2, Transceiver1.CSN
  N10: Arduino1.A1, Transceiver1.CE
  N11: Arduino1.D13, Transceiver1.SCK
  N12: Arduino1.D12, Transceiver1.MISO
  N13: Arduino1.D11_PWM, Transceiver1.MOSI
  N14: Arduino1.D10_PWM, S2.COM
  5V: Arduino1.5V, J1.Vcc, S2.L1, U1.output_voltage
  GND: Arduino1.GND, Transceiver1.GND, J1.GND, S1.leg0, S2.L2, U1.GND, VCC1.-, J2.pin1, LED1.cathode, LED2.cathode, LED3.cathode, LED4.cathode, LED5.cathode
  N15: Transceiver1.VCC, D1.A
  N16: D1.C, D2.A
  N17: D2.C, S1.leg1, R1.Pin_1
  N18: S3.COM, VCC1.+
  N19: S3.L2, U1.input_voltage
  N20: LED1.anode, R2.Pin_0
  N21: LED2.anode, R3.Pin_0
  N22: LED3.anode, R4.Pin_0
  N23: LED4.anode, R5.Pin_0
  N24: LED5.anode, R6.Pin_0

notes:
  470 Ohm
  7805
  10k
  1N4007
  NRFL24L01
  Arduino Pro Mini
  Sensor reflector Sharp GP2Y0A41SK0F

custom parts:
  nRF24L01: nRF24L01 module
